# Fritzing sketch Esquema de conexión (saved by Fritzing 0.9.4)
breadboards: 1

parts:
  Componente1 = Arduino Nano (Rev3.0)
  Componente2 = Adafruit VL53L0X Time of Flight Distance Sensor [part_number="Adafruit #3317"]
  Motor = Vibration Motor- ROB-08449 [package=vibe-motor-10mm]
  Pulsador = Pushbutton [package="[SMD]"]
  R1 = Resistor [tolerance=±5% resistance=220 package=THT]
  Buzzer = Piezo Speaker
  Led_RBG = RGB LED (com. cathode, rbg) [package="5 mm [THT]"]
  R2 = Resistor [tolerance=±5% resistance=220 package=THT]
  R3 = Resistor [tolerance=±5% resistance=10k package=THT]
  HC-SR04_Sensor_1 = HC-SR04 Ultrasonic Distance Sensor

nets (from the schematic view):
  GND: Componente1.GND, Componente2.GND, Motor.+, Buzzer.pin1, Led_RBG.common_cathode, R3.Pin_0, HC-SR04_Sensor_1.ECHO
  N1: Componente1.D4, Pulsador.Pin_1, Pulsador.Pin_2, R3.Pin_1
  N2: Componente1.D6, Buzzer.pin2
  N3: Componente1.D7, R2.Pin_0
  N4: Componente1.D8, R1.Pin_0
  N5: Componente1.D9, Motor.-
  N6: Componente1.D10, HC-SR04_Sensor_1.GND
  N7: Componente1.D11/MOSI, HC-SR04_Sensor_1.TRIG
  5V: Componente1.5V, Componente2.VIN, Pulsador.Pin_3, Pulsador.Pin_4, HC-SR04_Sensor_1.VCC
  N8: Componente1.A5, Componente2.SCL
  N9: Componente1.A4, Componente2.SDA
  N10: R1.Pin_1, Led_RBG.red_anode
  N11: Led_RBG.green_anode, R2.Pin_1

custom parts:
  Adafruit VL53L0X Time of Flight Distance Sensor: The VL53L0X is a Time of Flight distance sensor like no other you've used! The sensor contains a very tiny invisible laser source, and a matching sensor. The VL53L0X can detect the "time of flight", or how long the light has taken to bounce back to the sensor. Since it uses a very narrow light source, it is good for determining distance of only the surface directly in front of it. Unlike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
